// Logisim project 4bitadder.circ as structural Verilog: 1 circuit, main circuit main
module main (
);

  wire and_1_out, and_2_out, and_3_out, and_4_out, and_5_out, and_6_out, and_7_out, or_1_out, or_2_out,
       xor_2_out, xor_3_out, xor_6_out;
  wire [4:0] xor_1_out;

  and and_1 (and_1_out, 1'b1, 1'b1);
  xor xor_1 (xor_1_out[0], 1'b1, 1'b1);
  xor xor_2 (xor_2_out, 1'b0, 1'b1);
  xor xor_3 (xor_3_out, 1'b0, 1'b1);
  xor xor_4 (xor_1_out[1], xor_2_out, and_1_out);
  and and_2 (and_2_out, xor_2_out, and_1_out);
  and and_3 (and_3_out, 1'b0, 1'b1);
  xor xor_5 (xor_1_out[2], xor_3_out, or_1_out);
  and and_4 (and_4_out, xor_3_out, or_1_out);
  and and_5 (and_5_out, 1'b0, 1'b1);
  xor xor_6 (xor_6_out, 1'b1, 1'b0);
  xor xor_7 (xor_1_out[3], xor_6_out, or_2_out);
  and and_6 (and_6_out, xor_6_out, or_2_out);
  and and_7 (and_7_out, 1'b1, 1'b0);
  or or_1 (or_1_out, and_2_out, and_3_out);
  or or_2 (or_2_out, and_4_out, and_5_out);
  or or_3 (xor_1_out[4], and_6_out, and_7_out);
  // Probe on xor_1_out
endmodule
